// Logisim project ALU.circ as structural Verilog: 1 circuit, main circuit ALU
module ALU (
  input  in_1,
  input  in_2,
  input  [31:0] A,
  input  [31:0] B,
  input  [3:0] in_5,
  input  [3:0] in_6,
  input  [4:0] Shift,
  input  CarryIn,
  input  [3:0] Codop,
  output [3:0] Flags,
  output [31:0] S
);

  wire ASR, CMN, CMP, LSL, not_1_out, undriven, undriven_2, undriven_3, undriven_4, undriven_5;
  wire [4:0] subtractor_5_out, subtractor_6_out;
  wire [31:0] adder_1_out, adder_2_out, and_1_out, and_2_out, and_3_out, multiplier_1_out, not_2_out,
       not_3_out, or_1_out, shifter_1_out, shifter_2_out, shifter_3_out, shifter_4_out, subtractor_1_out,
       subtractor_2_out, subtractor_3_out, subtractor_4_out, xor_1_out;

  assign and_1_out = A & B;  // AND_Gate and_1, 32 bits wide
  assign xor_1_out = A ^ B;  // XOR_Gate xor_1, 32 bits wide
  Shifter #(.width(32)) shifter_1 (.in(B), .\dist (Shift), .out(shifter_1_out));
  Shifter #(.shift("lr"), .width(32)) shifter_2 (.in(B), .\dist (Shift), .out(shifter_2_out));
  Shifter #(.shift("ar"), .width(32)) shifter_3 (.in(B), .\dist (Shift), .out(shifter_3_out));
  Adder #(.width(32)) adder_1 (.a(A), .b(B), .out(adder_1_out), .cin(CarryIn));  // open: cout
  not not_1 (not_1_out, CarryIn);
  Subtractor #(.width(32)) subtractor_1 (.a(B), .b(A), .out(subtractor_1_out), .bin(not_1_out));  // open: bout
  Shifter #(.shift("rr"), .width(32)) shifter_4 (.in(B), .\dist (Shift), .out(shifter_4_out));
  assign and_2_out = A & B;  // AND_Gate and_2, 32 bits wide
  Subtractor #(.width(32)) subtractor_2 (.a({32{1'b0}}), .b(A), .out(subtractor_2_out), .bout(CMP));  // open: bin
  Subtractor #(.width(32)) subtractor_3 (.a(B), .b(A), .out(subtractor_3_out), .bout(CMN));  // open: bin
  Adder #(.width(32)) adder_2 (.a(A), .b(B), .out(adder_2_out));  // open: cin, cout
  assign or_1_out = A | B;  // OR_Gate or_1, 32 bits wide
  Multiplier #(.width(32)) multiplier_1 (.a(A), .b(B), .out(multiplier_1_out));  // open: cin, cout
  assign not_2_out = ~A;  // NOT_Gate not_2, 32 bits wide
  assign and_3_out = not_2_out & B;  // AND_Gate and_3, 32 bits wide
  assign not_3_out = ~A;  // NOT_Gate not_3, 32 bits wide
  Subtractor #(.width(32)) subtractor_4 (
    .a(subtractor_1_out), .b({32{1'b1}}), .out(subtractor_4_out));  // open: bin, bout
  Multiplexer #(.select(4), .width(32)) multiplexer_1 (
    .in0(and_1_out), .in1(xor_1_out), .in2(shifter_1_out), .in3(shifter_2_out), .in4(shifter_3_out),
    .in5(adder_1_out), .in6(subtractor_4_out), .in7(shifter_4_out), .in8(and_2_out), .in9(subtractor_2_out),
    .in10(subtractor_3_out), .in11(adder_2_out), .in12(or_1_out), .in13(multiplier_1_out), .in14(and_3_out),
    .in15(not_3_out), .out(S), .sel(Codop));
  Multiplexer #(.select(4)) multiplexer_2 (
    .in0(in_1), .in1(in_1), .in2(LSL), .in3(ASR), .in4(ASR), .in5(in_1), .in6(in_1), .in7(ASR), .in8(in_1),
    .in9(in_1), .in10(CMP), .in11(CMN), .in12(in_1), .in13(in_1), .in14(in_1), .in15(in_1), .out(Flags[2]),
    .sel(in_5));
  BitSelector #(.width(32)) bitselector_1 (.in(S), .out(Flags[0]), .sel({5{1'b1}}));
  Subtractor #(.width(5)) subtractor_5 (.a(Shift), .b(5'b00001), .out(subtractor_5_out));  // open: bin, bout
  BitSelector #(.width(32)) bitselector_2 (.in(B), .out(ASR), .sel(subtractor_5_out));
  BitSelector #(.width(32)) bitselector_3 (.in(B), .out(LSL), .sel(subtractor_6_out));
  Subtractor #(.width(5)) subtractor_6 (.a({5{1'b1}}), .b(Shift), .out(subtractor_6_out));  // open: bin, bout
  Comparator #(.width(32)) comparator_1 (.a(S), .b({32{1'b0}}), .eq(Flags[1]));  // open: gt, lt
  Multiplexer #(.select(4)) multiplexer_3 (
    .in0(in_2), .in1(in_2), .in2(in_2), .in3(in_2), .in4(in_2), .in5(undriven_4), .in6(undriven), .in7(in_2),
    .in8(in_2), .in9(undriven_2), .in10(undriven_3), .in11(undriven_5), .in12(in_2), .in13(in_2),
    .in14(in_2), .in15(in_2), .out(Flags[3]), .sel(in_6));

  // Other names for the same wires on the sheet: Negative = Flags[0]; Zero = Flags[1]; Carry = Flags[2];
  //   Overflow = Flags[3]; Res[31:0] = S; LSR = ASR; ROT = ASR; S_t[4:0] = Shift

  // Notes on the sheet:
  //   "1"
  //   "0"
  //   Note: for ROR, C = N
  //   Note 2: assume that shift > 0 for LSL and LSR
  //   A and B ?
  //   Gestion des Carry
  //   Negative
  //   Zero :
  //   Synthese des flags
  //   Xnor à faire entre les entrées A et B (dernier bit de chaque) et la sortie ( dernier bit) ( Si A et B sont positifs, alors le résultat doit etre positif)  
endmodule
