// Logisim project Ctl_Data_Processing.circ as structural Verilog: 1 circuit, main circuit Data_Processing
module Data_Processing (
  input  Enable,
  input  [15:0] Instruction,
  output [2:0] Rd,
  output [2:0] Rn,
  output [2:0] Rm,
  output [3:0] ALU_Opcode,
  output [3:0] Flags_Update_Mask
);

  wire [3:0] multiplexer_1_out;

  BitSelector #(.group(3), .width(16)) bitselector_1 (.in(Instruction), .out(Rd), .sel(3'b000));
  BitSelector #(.group(3), .width(16)) bitselector_2 (.in(Instruction), .out(Rm), .sel(3'b001));
  Multiplexer #(.select(4), .width(4)) multiplexer_1 (
    .in0(4'b0001), .in1(4'b0001), .in2(4'b0001), .in3(4'b0001), .in4(4'b0001), .in5(4'b0001), .in6(4'b0001),
    .in7(4'b0001), .in8(4'b0001), .in9(4'b0001), .in10(4'b0001), .in11(4'b0001), .in12(4'b0001),
    .in13(4'b0001), .in14(4'b0001), .in15(4'b0001), .out(multiplexer_1_out), .sel(ALU_Opcode));
  Multiplexer #(.width(4)) multiplexer_2 (
    .in0(4'b0000), .in1(multiplexer_1_out), .out(Flags_Update_Mask), .sel(Enable));

  assign Rn = Rd;

  // Other names for the same wires on the sheet: Flags[3:0] = Flags_Update_Mask; Opcode[3:0] = ALU_Opcode

  // Notes on the sheet:
  //   Choix de l'instruction
  //   Note 2: RSB instruction has Rn as 1st operand.
  //   MUL instruction has Rn as 1st operand and Rdm as 2nd operand
  //   For simplification purposes, Rm is used for 1st operand both here and in the ALU.
  //   Note: instructions that does not save the result will still have the second operand as the destination register, the ALU will copy the second register to the destination register
  //   Pull output low on Enable = 0
  //   Operandes A et B pour operation entre le contenu du registre Rdn et le contenu du registre Rm
endmodule
